# Fritzing sketch braike (saved by Fritzing 0.8.0b)
breadboards: 1

parts:
  Parte1 = Arduino Uno (Rev3)
  3-Axis_Accelerometer1 = 3-Axis Accelerometer Breakout - MMA8452Q

nets:
  N1: Parte1.A4/SDA, 3-Axis_Accelerometer1.SDA
  N2: Parte1.A5/SCL, 3-Axis_Accelerometer1.SCL
  GND: Parte1.GND, 3-Axis_Accelerometer1.GND
  N3: Parte1.D2, 3-Axis_Accelerometer1.I1
  N4: Parte1.D3_PWM, 3-Axis_Accelerometer1.I2
  3V3: Parte1.3V3, 3-Axis_Accelerometer1.3.3V
